// Logisim project main.circ as structural Verilog: 7 circuits, main circuit main
module main (
);

  wire clock_1_out;
  wire [6:0] keyboard_1_data;
  wire [7:0] keyboard_controller_1_x, keyboard_controller_1_y;

  Clock clock_1 (.out(clock_1_out));
  Keyboard keyboard_1 (.clk(clock_1_out), .re(1'b1), .data(keyboard_1_data));  // open: clr, avail
  Keyboard_controller keyboard_controller_1 (
    .ASCII_code(keyboard_1_data), .X(keyboard_controller_1_x), .Y(keyboard_controller_1_y));
  // Probe on keyboard_controller_1_x
  // Probe on keyboard_controller_1_y

  // Notes on the sheet:
  //   Keyboard
endmodule

module _16_16_matrix (
  input  [7:0] Lo_byte,
  input  Lo_byte_on,
  input  [7:0] Hi_byte,
  input  Hi_byte_On,
  input  [7:0] Selector,
  input  Selection_On,
  input  Bus_0
);

  wire clk, demultiplexer_1_out0, demultiplexer_1_out1, demultiplexer_1_out2, demultiplexer_1_out3,
       demultiplexer_1_out4, demultiplexer_1_out5, demultiplexer_1_out6, demultiplexer_1_out7,
       demultiplexer_1_out8, demultiplexer_1_out9, demultiplexer_1_out10, demultiplexer_1_out11,
       demultiplexer_1_out12, demultiplexer_1_out13, demultiplexer_1_out14, demultiplexer_1_out15;
  wire [7:0] register_1_q, register_2_q, register_3_q;
  wire [15:0] register_4_q, register_5_q, register_6_q, register_7_q, register_8_q, register_9_q,
       register_10_q, register_11_q, register_12_q, register_13_q, register_14_q, register_15_q,
       register_16_q, register_17_q, register_18_q, register_19_q;

  Clock clock_1 (.out(clk));
  Register register_1 (.D(Lo_byte), .en(Lo_byte_on), .Q(register_1_q), .clk(clk));  // open: clr
  Register register_2 (.D(Hi_byte), .en(Hi_byte_On), .Q(register_2_q), .clk(clk));  // open: clr
  Register #(.trigger("high")) register_3 (.D(Selector), .en(Selection_On), .Q(register_3_q), .clk(clk));  // open: clr
  // Probe on register_3_q
  Demultiplexer #(.select(4), .disabled(0)) demultiplexer_1 (
    .out0(demultiplexer_1_out0), .out1(demultiplexer_1_out1), .out2(demultiplexer_1_out2),
    .out3(demultiplexer_1_out3), .out4(demultiplexer_1_out4), .out5(demultiplexer_1_out5),
    .out6(demultiplexer_1_out6), .out7(demultiplexer_1_out7), .out8(demultiplexer_1_out8),
    .out9(demultiplexer_1_out9), .out10(demultiplexer_1_out10), .out11(demultiplexer_1_out11),
    .out12(demultiplexer_1_out12), .out13(demultiplexer_1_out13), .out14(demultiplexer_1_out14),
    .out15(demultiplexer_1_out15), .in(Selection_On), .sel(register_3_q[3:0]), .en(Selection_On));
  Register #(.width(16)) register_4 (
    .D({register_2_q, register_1_q}), .en(demultiplexer_1_out0), .Q(register_4_q), .clk(clk));  // open: clr
  Register #(.width(16)) register_5 (
    .D({register_2_q, register_1_q}), .en(demultiplexer_1_out1), .Q(register_5_q), .clk(clk));  // open: clr
  Register #(.width(16)) register_6 (
    .D({register_2_q, register_1_q}), .en(demultiplexer_1_out2), .Q(register_6_q), .clk(clk));  // open: clr
  Register #(.width(16)) register_7 (
    .D({register_2_q, register_1_q}), .en(demultiplexer_1_out3), .Q(register_7_q), .clk(clk));  // open: clr
  Register #(.width(16)) register_8 (
    .D({register_2_q, register_1_q}), .en(demultiplexer_1_out4), .Q(register_8_q), .clk(clk));  // open: clr
  Register #(.width(16)) register_9 (
    .D({register_2_q, register_1_q}), .en(demultiplexer_1_out5), .Q(register_9_q), .clk(clk));  // open: clr
  Register #(.width(16)) register_10 (
    .D({register_2_q, register_1_q}), .en(demultiplexer_1_out6), .Q(register_10_q), .clk(clk));  // open: clr
  Register #(.width(16)) register_11 (
    .D({register_2_q, register_1_q}), .en(demultiplexer_1_out7), .Q(register_11_q), .clk(clk));  // open: clr
  Register #(.width(16)) register_12 (
    .D({register_2_q, register_1_q}), .en(demultiplexer_1_out8), .Q(register_12_q), .clk(clk));  // open: clr
  Register #(.width(16)) register_13 (
    .D({register_2_q, register_1_q}), .en(demultiplexer_1_out9), .Q(register_13_q), .clk(clk));  // open: clr
  Register #(.width(16)) register_14 (
    .D({register_2_q, register_1_q}), .en(demultiplexer_1_out10), .Q(register_14_q), .clk(clk));  // open: clr
  Register #(.width(16)) register_15 (
    .D({register_2_q, register_1_q}), .en(demultiplexer_1_out11), .Q(register_15_q), .clk(clk));  // open: clr
  Register #(.width(16)) register_16 (
    .D({register_2_q, register_1_q}), .en(demultiplexer_1_out12), .Q(register_16_q), .clk(clk));  // open: clr
  Register #(.width(16)) register_17 (
    .D({register_2_q, register_1_q}), .en(demultiplexer_1_out13), .Q(register_17_q), .clk(clk));  // open: clr
  Register #(.width(16)) register_18 (
    .D({register_2_q, register_1_q}), .en(demultiplexer_1_out14), .Q(register_18_q), .clk(clk));  // open: clr
  Register #(.width(16)) register_19 (
    .D({register_2_q, register_1_q}), .en(demultiplexer_1_out15), .Q(register_19_q), .clk(clk));  // open: clr
  DotMatrix #(.inputtype("row"), .matrixcols(16), .matrixrows(16)) dotmatrix_1 (
    .row0(register_4_q), .row1(register_5_q), .row2(register_6_q), .row3(register_7_q), .row4(register_8_q),
    .row5(register_9_q), .row6(register_10_q), .row7(register_11_q), .row8(register_12_q),
    .row9(register_13_q), .row10(register_14_q), .row11(register_15_q), .row12(register_16_q),
    .row13(register_17_q), .row14(register_18_q), .row15(register_19_q));
endmodule

module _16_16_demonstration (
  input  Full_On,
  input  Selection_On,
  input  Bus_0
);

  wire clk, demultiplexer_1_out0, demultiplexer_1_out1, demultiplexer_1_out2, demultiplexer_1_out3,
       demultiplexer_1_out4, demultiplexer_1_out5, demultiplexer_1_out6, demultiplexer_1_out7,
       demultiplexer_1_out8, demultiplexer_1_out9, demultiplexer_1_out10, demultiplexer_1_out11,
       demultiplexer_1_out12, demultiplexer_1_out13, demultiplexer_1_out14, demultiplexer_1_out15, rst;
  wire [3:0] random_1_out;
  wire [15:0] random_2_out, register_1_q, register_2_q, register_3_q, register_4_q, register_5_q,
       register_6_q, register_7_q, register_8_q, register_9_q, register_10_q, register_11_q, register_12_q,
       register_13_q, register_14_q, register_15_q, register_16_q;

  Clock clock_1 (.out(clk));
  Button Reset (.out(rst));
  Demultiplexer #(.select(4), .disabled(0)) demultiplexer_1 (
    .out0(demultiplexer_1_out0), .out1(demultiplexer_1_out1), .out2(demultiplexer_1_out2),
    .out3(demultiplexer_1_out3), .out4(demultiplexer_1_out4), .out5(demultiplexer_1_out5),
    .out6(demultiplexer_1_out6), .out7(demultiplexer_1_out7), .out8(demultiplexer_1_out8),
    .out9(demultiplexer_1_out9), .out10(demultiplexer_1_out10), .out11(demultiplexer_1_out11),
    .out12(demultiplexer_1_out12), .out13(demultiplexer_1_out13), .out14(demultiplexer_1_out14),
    .out15(demultiplexer_1_out15), .in(Selection_On), .sel(random_1_out), .en(Selection_On));
  Random #(.width(4)) random_1 (.clk(clk), .next(Full_On), .out(random_1_out), .clr(rst));
  Random #(.width(16), .seed(5)) random_2 (.clk(clk), .next(Full_On), .out(random_2_out), .clr(rst));
  Register #(.width(16)) register_1 (
    .D(random_2_out), .en(demultiplexer_1_out0), .Q(register_1_q), .clk(clk), .clr(rst));
  Register #(.width(16)) register_2 (
    .D(random_2_out), .en(demultiplexer_1_out1), .Q(register_2_q), .clk(clk), .clr(rst));
  Register #(.width(16)) register_3 (
    .D(random_2_out), .en(demultiplexer_1_out2), .Q(register_3_q), .clk(clk), .clr(rst));
  Register #(.width(16)) register_4 (
    .D(random_2_out), .en(demultiplexer_1_out3), .Q(register_4_q), .clk(clk), .clr(rst));
  Register #(.width(16)) register_5 (
    .D(random_2_out), .en(demultiplexer_1_out4), .Q(register_5_q), .clk(clk), .clr(rst));
  Register #(.width(16)) register_6 (
    .D(random_2_out), .en(demultiplexer_1_out5), .Q(register_6_q), .clk(clk), .clr(rst));
  Register #(.width(16)) register_7 (
    .D(random_2_out), .en(demultiplexer_1_out6), .Q(register_7_q), .clk(clk), .clr(rst));
  Register #(.width(16)) register_8 (
    .D(random_2_out), .en(demultiplexer_1_out7), .Q(register_8_q), .clk(clk), .clr(rst));
  Register #(.width(16)) register_9 (
    .D(random_2_out), .en(demultiplexer_1_out8), .Q(register_9_q), .clk(clk), .clr(rst));
  Register #(.width(16)) register_10 (
    .D(random_2_out), .en(demultiplexer_1_out9), .Q(register_10_q), .clk(clk), .clr(rst));
  Register #(.width(16)) register_11 (
    .D(random_2_out), .en(demultiplexer_1_out10), .Q(register_11_q), .clk(clk), .clr(rst));
  Register #(.width(16)) register_12 (
    .D(random_2_out), .en(demultiplexer_1_out11), .Q(register_12_q), .clk(clk), .clr(rst));
  Register #(.width(16)) register_13 (
    .D(random_2_out), .en(demultiplexer_1_out12), .Q(register_13_q), .clk(clk), .clr(rst));
  Register #(.width(16)) register_14 (
    .D(random_2_out), .en(demultiplexer_1_out13), .Q(register_14_q), .clk(clk), .clr(rst));
  Register #(.width(16)) register_15 (
    .D(random_2_out), .en(demultiplexer_1_out14), .Q(register_15_q), .clk(clk), .clr(rst));
  Register #(.width(16)) register_16 (
    .D(random_2_out), .en(demultiplexer_1_out15), .Q(register_16_q), .clk(clk), .clr(rst));
  DotMatrix #(.inputtype("row"), .matrixcols(16), .matrixrows(16)) dotmatrix_1 (
    .row0(register_1_q), .row1(register_2_q), .row2(register_3_q), .row3(register_4_q), .row4(register_5_q),
    .row5(register_6_q), .row6(register_7_q), .row7(register_8_q), .row8(register_9_q), .row9(register_10_q),
    .row10(register_11_q), .row11(register_12_q), .row12(register_13_q), .row13(register_14_q),
    .row14(register_15_q), .row15(register_16_q));

  // Other names for the same wires on the sheet: on = Full_On
endmodule

module _32_32_matrix (
  input  [7:0] _0_byte,
  input  _0_byte_on,
  input  [7:0] _1_byte,
  input  _1_byte_On,
  input  [7:0] _2_byte,
  input  _2_byte_on,
  input  [7:0] _3_byte,
  input  _3_byte_On,
  input  [7:0] Selector,
  input  Selection_On,
  input  Bus_0
);

  wire clk, demultiplexer_1_out0, demultiplexer_1_out1, demultiplexer_1_out2, demultiplexer_1_out3,
       demultiplexer_1_out4, demultiplexer_1_out5, demultiplexer_1_out6, demultiplexer_1_out7,
       demultiplexer_1_out8, demultiplexer_1_out9, demultiplexer_1_out10, demultiplexer_1_out11,
       demultiplexer_1_out12, demultiplexer_1_out13, demultiplexer_1_out14, demultiplexer_1_out15,
       demultiplexer_1_out16, demultiplexer_1_out17, demultiplexer_1_out18, demultiplexer_1_out19,
       demultiplexer_1_out20, demultiplexer_1_out21, demultiplexer_1_out22, demultiplexer_1_out23,
       demultiplexer_1_out24, demultiplexer_1_out25, demultiplexer_1_out26, demultiplexer_1_out27,
       demultiplexer_1_out28, demultiplexer_1_out29, demultiplexer_1_out30, demultiplexer_1_out31;
  wire [7:0] register_1_q, register_2_q, register_3_q, register_4_q, register_5_q;
  wire [31:0] register_6_q, register_7_q, register_8_q, register_9_q, register_10_q, register_11_q,
       register_12_q, register_13_q, register_14_q, register_15_q, register_16_q, register_17_q,
       register_18_q, register_19_q, register_20_q, register_21_q, register_22_q, register_23_q,
       register_24_q, register_25_q, register_26_q, register_27_q, register_28_q, register_29_q,
       register_30_q, register_31_q, register_32_q, register_33_q, register_34_q, register_35_q,
       register_36_q, register_37_q;

  Clock clock_1 (.out(clk));
  Register register_1 (.D(_0_byte), .en(_0_byte_on), .Q(register_1_q), .clk(clk));  // open: clr
  Register register_2 (.D(_1_byte), .en(_1_byte_On), .Q(register_2_q), .clk(clk));  // open: clr
  Register register_3 (.D(_2_byte), .en(_2_byte_on), .Q(register_3_q), .clk(clk));  // open: clr
  Register register_4 (.D(_3_byte), .en(_3_byte_On), .Q(register_4_q), .clk(clk));  // open: clr
  Register #(.trigger("high")) register_5 (.D(Selector), .en(Selection_On), .Q(register_5_q), .clk(clk));  // open: clr
  // Probe on register_5_q
  Demultiplexer #(.select(5), .disabled(0)) demultiplexer_1 (
    .out0(demultiplexer_1_out0), .out1(demultiplexer_1_out1), .out2(demultiplexer_1_out2),
    .out3(demultiplexer_1_out3), .out4(demultiplexer_1_out4), .out5(demultiplexer_1_out5),
    .out6(demultiplexer_1_out6), .out7(demultiplexer_1_out7), .out8(demultiplexer_1_out8),
    .out9(demultiplexer_1_out9), .out10(demultiplexer_1_out10), .out11(demultiplexer_1_out11),
    .out12(demultiplexer_1_out12), .out13(demultiplexer_1_out13), .out14(demultiplexer_1_out14),
    .out15(demultiplexer_1_out15), .out16(demultiplexer_1_out16), .out17(demultiplexer_1_out17),
    .out18(demultiplexer_1_out18), .out19(demultiplexer_1_out19), .out20(demultiplexer_1_out20),
    .out21(demultiplexer_1_out21), .out22(demultiplexer_1_out22), .out23(demultiplexer_1_out23),
    .out24(demultiplexer_1_out24), .out25(demultiplexer_1_out25), .out26(demultiplexer_1_out26),
    .out27(demultiplexer_1_out27), .out28(demultiplexer_1_out28), .out29(demultiplexer_1_out29),
    .out30(demultiplexer_1_out30), .out31(demultiplexer_1_out31), .in(Selection_On), .sel(register_5_q[4:0]));  // open: en
  Register #(.width(32)) register_6 (
    .D({register_4_q, register_3_q, register_2_q, register_1_q}), .en(demultiplexer_1_out0),
    .Q(register_6_q), .clk(clk));  // open: clr
  Register #(.width(32)) register_7 (
    .D({register_4_q, register_3_q, register_2_q, register_1_q}), .en(demultiplexer_1_out1),
    .Q(register_7_q), .clk(clk));  // open: clr
  Register #(.width(32)) register_8 (
    .D({register_4_q, register_3_q, register_2_q, register_1_q}), .en(demultiplexer_1_out2),
    .Q(register_8_q), .clk(clk));  // open: clr
  Register #(.width(32)) register_9 (
    .D({register_4_q, register_3_q, register_2_q, register_1_q}), .en(demultiplexer_1_out3),
    .Q(register_9_q), .clk(clk));  // open: clr
  Register #(.width(32)) register_10 (
    .D({register_4_q, register_3_q, register_2_q, register_1_q}), .en(demultiplexer_1_out4),
    .Q(register_10_q), .clk(clk));  // open: clr
  Register #(.width(32)) register_11 (
    .D({register_4_q, register_3_q, register_2_q, register_1_q}), .en(demultiplexer_1_out5),
    .Q(register_11_q), .clk(clk));  // open: clr
  Register #(.width(32)) register_12 (
    .D({register_4_q, register_3_q, register_2_q, register_1_q}), .en(demultiplexer_1_out6),
    .Q(register_12_q), .clk(clk));  // open: clr
  Register #(.width(32)) register_13 (
    .D({register_4_q, register_3_q, register_2_q, register_1_q}), .en(demultiplexer_1_out7),
    .Q(register_13_q), .clk(clk));  // open: clr
  Register #(.width(32)) register_14 (
    .D({register_4_q, register_3_q, register_2_q, register_1_q}), .en(demultiplexer_1_out8),
    .Q(register_14_q), .clk(clk));  // open: clr
  Register #(.width(32)) register_15 (
    .D({register_4_q, register_3_q, register_2_q, register_1_q}), .en(demultiplexer_1_out9),
    .Q(register_15_q), .clk(clk));  // open: clr
  Register #(.width(32)) register_16 (
    .D({register_4_q, register_3_q, register_2_q, register_1_q}), .en(demultiplexer_1_out10),
    .Q(register_16_q), .clk(clk));  // open: clr
  Register #(.width(32)) register_17 (
    .D({register_4_q, register_3_q, register_2_q, register_1_q}), .en(demultiplexer_1_out11),
    .Q(register_17_q), .clk(clk));  // open: clr
  Register #(.width(32)) register_18 (
    .D({register_4_q, register_3_q, register_2_q, register_1_q}), .en(demultiplexer_1_out12),
    .Q(register_18_q), .clk(clk));  // open: clr
  Register #(.width(32)) register_19 (
    .D({register_4_q, register_3_q, register_2_q, register_1_q}), .en(demultiplexer_1_out13),
    .Q(register_19_q), .clk(clk));  // open: clr
  Register #(.width(32)) register_20 (
    .D({register_4_q, register_3_q, register_2_q, register_1_q}), .en(demultiplexer_1_out14),
    .Q(register_20_q), .clk(clk));  // open: clr
  Register #(.width(32)) register_21 (
    .D({register_4_q, register_3_q, register_2_q, register_1_q}), .en(demultiplexer_1_out15),
    .Q(register_21_q), .clk(clk));  // open: clr
  Register #(.width(32)) register_22 (
    .D({register_4_q, register_3_q, register_2_q, register_1_q}), .en(demultiplexer_1_out16),
    .Q(register_22_q), .clk(clk));  // open: clr
  Register #(.width(32)) register_23 (
    .D({register_4_q, register_3_q, register_2_q, register_1_q}), .en(demultiplexer_1_out17),
    .Q(register_23_q), .clk(clk));  // open: clr
  Register #(.width(32)) register_24 (
    .D({register_4_q, register_3_q, register_2_q, register_1_q}), .en(demultiplexer_1_out18),
    .Q(register_24_q), .clk(clk));  // open: clr
  Register #(.width(32)) register_25 (
    .D({register_4_q, register_3_q, register_2_q, register_1_q}), .en(demultiplexer_1_out19),
    .Q(register_25_q), .clk(clk));  // open: clr
  Register #(.width(32)) register_26 (
    .D({register_4_q, register_3_q, register_2_q, register_1_q}), .en(demultiplexer_1_out20),
    .Q(register_26_q), .clk(clk));  // open: clr
  Register #(.width(32)) register_27 (
    .D({register_4_q, register_3_q, register_2_q, register_1_q}), .en(demultiplexer_1_out21),
    .Q(register_27_q), .clk(clk));  // open: clr
  Register #(.width(32)) register_28 (
    .D({register_4_q, register_3_q, register_2_q, register_1_q}), .en(demultiplexer_1_out22),
    .Q(register_28_q), .clk(clk));  // open: clr
  Register #(.width(32)) register_29 (
    .D({register_4_q, register_3_q, register_2_q, register_1_q}), .en(demultiplexer_1_out23),
    .Q(register_29_q), .clk(clk));  // open: clr
  Register #(.width(32)) register_30 (
    .D({register_4_q, register_3_q, register_2_q, register_1_q}), .en(demultiplexer_1_out24),
    .Q(register_30_q), .clk(clk));  // open: clr
  Register #(.width(32)) register_31 (
    .D({register_4_q, register_3_q, register_2_q, register_1_q}), .en(demultiplexer_1_out25),
    .Q(register_31_q), .clk(clk));  // open: clr
  Register #(.width(32)) register_32 (
    .D({register_4_q, register_3_q, register_2_q, register_1_q}), .en(demultiplexer_1_out26),
    .Q(register_32_q), .clk(clk));  // open: clr
  Register #(.width(32)) register_33 (
    .D({register_4_q, register_3_q, register_2_q, register_1_q}), .en(demultiplexer_1_out27),
    .Q(register_33_q), .clk(clk));  // open: clr
  Register #(.width(32)) register_34 (
    .D({register_4_q, register_3_q, register_2_q, register_1_q}), .en(demultiplexer_1_out28),
    .Q(register_34_q), .clk(clk));  // open: clr
  Register #(.width(32)) register_35 (
    .D({register_4_q, register_3_q, register_2_q, register_1_q}), .en(demultiplexer_1_out29),
    .Q(register_35_q), .clk(clk));  // open: clr
  Register #(.width(32)) register_36 (
    .D({register_4_q, register_3_q, register_2_q, register_1_q}), .en(demultiplexer_1_out30),
    .Q(register_36_q), .clk(clk));  // open: clr
  Register #(.width(32)) register_37 (
    .D({register_4_q, register_3_q, register_2_q, register_1_q}), .en(demultiplexer_1_out31),
    .Q(register_37_q), .clk(clk));  // open: clr
  DotMatrix #(.inputtype("row"), .matrixcols(32), .matrixrows(32)) dotmatrix_1 (
    .row0(register_6_q), .row1(register_7_q), .row2(register_8_q), .row3(register_9_q), .row4(register_10_q),
    .row5(register_11_q), .row6(register_12_q), .row7(register_13_q), .row8(register_14_q),
    .row9(register_15_q), .row10(register_16_q), .row11(register_17_q), .row12(register_18_q),
    .row13(register_19_q), .row14(register_20_q), .row15(register_21_q), .row16(register_22_q),
    .row17(register_23_q), .row18(register_24_q), .row19(register_25_q), .row20(register_26_q),
    .row21(register_27_q), .row22(register_28_q), .row23(register_29_q), .row24(register_30_q),
    .row25(register_31_q), .row26(register_32_q), .row27(register_33_q), .row28(register_34_q),
    .row29(register_35_q), .row30(register_36_q), .row31(register_37_q));
endmodule

module _32_32_demo (
  input  Full_On,
  input  Selection_On,
  input  Bus_0
);

  wire clk;
  wire [7:0] random_1_out, random_2_out;
  wire [31:0] n32_32_buffer_1_out_13, n32_32_buffer_1_out_14, n32_32_buffer_1_out_15, n32_32_buffer_1_out_16,
       n32_32_buffer_1_out_17, n32_32_buffer_1_out_18, n32_32_buffer_1_out_19, n32_32_buffer_1_out_20,
       n32_32_buffer_1_out_21, n32_32_buffer_1_out_22, n32_32_buffer_1_out_23, n32_32_buffer_1_out_24,
       n32_32_buffer_1_out_25, n32_32_buffer_1_out_26, n32_32_buffer_1_out_27, n32_32_buffer_1_out_28,
       n32_32_buffer_1_out_30, n32_32_buffer_1_out_31, n32_32_buffer_1_out_32, n32_32_buffer_1_out_33,
       n32_32_buffer_1_out_34, n32_32_buffer_1_out_35, n32_32_buffer_1_out_36, n32_32_buffer_1_out_37,
       n32_32_buffer_1_out_38, n32_32_buffer_1_out_39, n32_32_buffer_1_out_40, n32_32_buffer_1_out_41,
       n32_32_buffer_1_out_42, n32_32_buffer_1_out_43, n32_32_buffer_1_out_44, n32_32_buffer_1_out_45;

  Clock clock_1 (.out(clk));
  Random #(.seed(10)) random_1 (.clk(clk), .next(Full_On), .out(random_1_out));  // open: clr
  Random random_2 (.clk(clk), .next(Full_On), .out(random_2_out));  // open: clr
  _32_32_buffer u_32_32_buffer_1 (
    ._0_byte(random_1_out), ._0_byte_on(Full_On), ._1_byte(random_1_out), ._1_byte_On(Full_On),
    ._2_byte(random_1_out), ._2_byte_on(Full_On), ._3_byte(random_1_out), ._3_byte_On(Full_On),
    .Selector(random_2_out), .Selection_On(Selection_On), .out_13(n32_32_buffer_1_out_13),
    .out_14(n32_32_buffer_1_out_14), .out_15(n32_32_buffer_1_out_15), .out_16(n32_32_buffer_1_out_16),
    .out_17(n32_32_buffer_1_out_17), .out_18(n32_32_buffer_1_out_18), .out_19(n32_32_buffer_1_out_19),
    .out_20(n32_32_buffer_1_out_20), .out_21(n32_32_buffer_1_out_21), .out_22(n32_32_buffer_1_out_22),
    .out_23(n32_32_buffer_1_out_23), .out_24(n32_32_buffer_1_out_24), .out_25(n32_32_buffer_1_out_25),
    .out_26(n32_32_buffer_1_out_26), .out_27(n32_32_buffer_1_out_27), .out_28(n32_32_buffer_1_out_28),
    .out_30(n32_32_buffer_1_out_30), .out_31(n32_32_buffer_1_out_31), .out_32(n32_32_buffer_1_out_32),
    .out_33(n32_32_buffer_1_out_33), .out_34(n32_32_buffer_1_out_34), .out_35(n32_32_buffer_1_out_35),
    .out_36(n32_32_buffer_1_out_36), .out_37(n32_32_buffer_1_out_37), .out_38(n32_32_buffer_1_out_38),
    .out_39(n32_32_buffer_1_out_39), .out_40(n32_32_buffer_1_out_40), .out_41(n32_32_buffer_1_out_41),
    .out_42(n32_32_buffer_1_out_42), .out_43(n32_32_buffer_1_out_43), .out_44(n32_32_buffer_1_out_44),
    .out_45(n32_32_buffer_1_out_45));  // open: Bus_0, Single_row_output, Output_Selector
  DotMatrix #(.inputtype("row"), .matrixcols(32), .matrixrows(32)) dotmatrix_1 (
    .row0(n32_32_buffer_1_out_13), .row1(n32_32_buffer_1_out_14), .row2(n32_32_buffer_1_out_15),
    .row3(n32_32_buffer_1_out_16), .row4(n32_32_buffer_1_out_17), .row5(n32_32_buffer_1_out_18),
    .row6(n32_32_buffer_1_out_19), .row7(n32_32_buffer_1_out_20), .row8(n32_32_buffer_1_out_21),
    .row9(n32_32_buffer_1_out_22), .row10(n32_32_buffer_1_out_23), .row11(n32_32_buffer_1_out_24),
    .row12(n32_32_buffer_1_out_25), .row13(n32_32_buffer_1_out_26), .row14(n32_32_buffer_1_out_27),
    .row15(n32_32_buffer_1_out_28), .row16(n32_32_buffer_1_out_30), .row17(n32_32_buffer_1_out_31),
    .row18(n32_32_buffer_1_out_32), .row19(n32_32_buffer_1_out_33), .row20(n32_32_buffer_1_out_34),
    .row21(n32_32_buffer_1_out_35), .row22(n32_32_buffer_1_out_36), .row23(n32_32_buffer_1_out_37),
    .row24(n32_32_buffer_1_out_38), .row25(n32_32_buffer_1_out_39), .row26(n32_32_buffer_1_out_40),
    .row27(n32_32_buffer_1_out_41), .row28(n32_32_buffer_1_out_42), .row29(n32_32_buffer_1_out_43),
    .row30(n32_32_buffer_1_out_44), .row31(n32_32_buffer_1_out_45));

  // Other names for the same wires on the sheet: on = Full_On
endmodule

module _32_32_buffer (
  input  [7:0] _0_byte,
  input  _0_byte_on,
  input  [7:0] _1_byte,
  input  _1_byte_On,
  input  [7:0] _2_byte,
  input  _2_byte_on,
  input  [7:0] _3_byte,
  input  _3_byte_On,
  input  [7:0] Selector,
  input  Selection_On,
  input  [7:0] Output_Selector,
  input  Bus_0,
  output [31:0] out_13,
  output [31:0] out_14,
  output [31:0] out_15,
  output [31:0] out_16,
  output [31:0] out_17,
  output [31:0] out_18,
  output [31:0] out_19,
  output [31:0] out_20,
  output [31:0] out_21,
  output [31:0] out_22,
  output [31:0] out_23,
  output [31:0] out_24,
  output [31:0] out_25,
  output [31:0] out_26,
  output [31:0] out_27,
  output [31:0] out_28,
  output [31:0] Single_row_output,
  output [31:0] out_30,
  output [31:0] out_31,
  output [31:0] out_32,
  output [31:0] out_33,
  output [31:0] out_34,
  output [31:0] out_35,
  output [31:0] out_36,
  output [31:0] out_37,
  output [31:0] out_38,
  output [31:0] out_39,
  output [31:0] out_40,
  output [31:0] out_41,
  output [31:0] out_42,
  output [31:0] out_43,
  output [31:0] out_44,
  output [31:0] out_45
);

  wire clk, demultiplexer_1_out0, demultiplexer_1_out1, demultiplexer_1_out2, demultiplexer_1_out3,
       demultiplexer_1_out4, demultiplexer_1_out5, demultiplexer_1_out6, demultiplexer_1_out7,
       demultiplexer_1_out8, demultiplexer_1_out9, demultiplexer_1_out10, demultiplexer_1_out11,
       demultiplexer_1_out12, demultiplexer_1_out13, demultiplexer_1_out14, demultiplexer_1_out15,
       demultiplexer_1_out16, demultiplexer_1_out17, demultiplexer_1_out18, demultiplexer_1_out19,
       demultiplexer_1_out20, demultiplexer_1_out21, demultiplexer_1_out22, demultiplexer_1_out23,
       demultiplexer_1_out24, demultiplexer_1_out25, demultiplexer_1_out26, demultiplexer_1_out27,
       demultiplexer_1_out28, demultiplexer_1_out29, demultiplexer_1_out30, demultiplexer_1_out31;
  wire [7:0] register_1_q, register_2_q, register_3_q, register_4_q, register_5_q;

  Clock clock_1 (.out(clk));
  Register register_1 (.D(_0_byte), .en(_0_byte_on), .Q(register_1_q), .clk(clk));  // open: clr
  Register register_2 (.D(_1_byte), .en(_1_byte_On), .Q(register_2_q), .clk(clk));  // open: clr
  Register register_3 (.D(_2_byte), .en(_2_byte_on), .Q(register_3_q), .clk(clk));  // open: clr
  Register register_4 (.D(_3_byte), .en(_3_byte_On), .Q(register_4_q), .clk(clk));  // open: clr
  Register #(.trigger("high")) register_5 (.D(Selector), .en(Selection_On), .Q(register_5_q), .clk(clk));  // open: clr
  // Probe on register_5_q
  Demultiplexer #(.select(5), .disabled(0), .enable("false")) demultiplexer_1 (
    .out0(demultiplexer_1_out0), .out1(demultiplexer_1_out1), .out2(demultiplexer_1_out2),
    .out3(demultiplexer_1_out3), .out4(demultiplexer_1_out4), .out5(demultiplexer_1_out5),
    .out6(demultiplexer_1_out6), .out7(demultiplexer_1_out7), .out8(demultiplexer_1_out8),
    .out9(demultiplexer_1_out9), .out10(demultiplexer_1_out10), .out11(demultiplexer_1_out11),
    .out12(demultiplexer_1_out12), .out13(demultiplexer_1_out13), .out14(demultiplexer_1_out14),
    .out15(demultiplexer_1_out15), .out16(demultiplexer_1_out16), .out17(demultiplexer_1_out17),
    .out18(demultiplexer_1_out18), .out19(demultiplexer_1_out19), .out20(demultiplexer_1_out20),
    .out21(demultiplexer_1_out21), .out22(demultiplexer_1_out22), .out23(demultiplexer_1_out23),
    .out24(demultiplexer_1_out24), .out25(demultiplexer_1_out25), .out26(demultiplexer_1_out26),
    .out27(demultiplexer_1_out27), .out28(demultiplexer_1_out28), .out29(demultiplexer_1_out29),
    .out30(demultiplexer_1_out30), .out31(demultiplexer_1_out31), .in(Selection_On), .sel(register_5_q[4:0]));
  Register #(.width(32)) register_6 (
    .D({register_4_q, register_3_q, register_2_q, register_1_q}), .en(demultiplexer_1_out0), .Q(out_13),
    .clk(clk));  // open: clr
  Register #(.width(32)) register_7 (
    .D({register_4_q, register_3_q, register_2_q, register_1_q}), .en(demultiplexer_1_out1), .Q(out_14),
    .clk(clk));  // open: clr
  Register #(.width(32)) register_8 (
    .D({register_4_q, register_3_q, register_2_q, register_1_q}), .en(demultiplexer_1_out2), .Q(out_15),
    .clk(clk));  // open: clr
  Register #(.width(32)) register_9 (
    .D({register_4_q, register_3_q, register_2_q, register_1_q}), .en(demultiplexer_1_out3), .Q(out_16),
    .clk(clk));  // open: clr
  Register #(.width(32)) register_10 (
    .D({register_4_q, register_3_q, register_2_q, register_1_q}), .en(demultiplexer_1_out4), .Q(out_17),
    .clk(clk));  // open: clr
  Register #(.width(32)) register_11 (
    .D({register_4_q, register_3_q, register_2_q, register_1_q}), .en(demultiplexer_1_out5), .Q(out_18),
    .clk(clk));  // open: clr
  Register #(.width(32)) register_12 (
    .D({register_4_q, register_3_q, register_2_q, register_1_q}), .en(demultiplexer_1_out6), .Q(out_19),
    .clk(clk));  // open: clr
  Register #(.width(32)) register_13 (
    .D({register_4_q, register_3_q, register_2_q, register_1_q}), .en(demultiplexer_1_out7), .Q(out_20),
    .clk(clk));  // open: clr
  Register #(.width(32)) register_14 (
    .D({register_4_q, register_3_q, register_2_q, register_1_q}), .en(demultiplexer_1_out8), .Q(out_21),
    .clk(clk));  // open: clr
  Register #(.width(32)) register_15 (
    .D({register_4_q, register_3_q, register_2_q, register_1_q}), .en(demultiplexer_1_out9), .Q(out_22),
    .clk(clk));  // open: clr
  Register #(.width(32)) register_16 (
    .D({register_4_q, register_3_q, register_2_q, register_1_q}), .en(demultiplexer_1_out10), .Q(out_23),
    .clk(clk));  // open: clr
  Register #(.width(32)) register_17 (
    .D({register_4_q, register_3_q, register_2_q, register_1_q}), .en(demultiplexer_1_out11), .Q(out_24),
    .clk(clk));  // open: clr
  Register #(.width(32)) register_18 (
    .D({register_4_q, register_3_q, register_2_q, register_1_q}), .en(demultiplexer_1_out12), .Q(out_25),
    .clk(clk));  // open: clr
  Register #(.width(32)) register_19 (
    .D({register_4_q, register_3_q, register_2_q, register_1_q}), .en(demultiplexer_1_out13), .Q(out_26),
    .clk(clk));  // open: clr
  Register #(.width(32)) register_20 (
    .D({register_4_q, register_3_q, register_2_q, register_1_q}), .en(demultiplexer_1_out14), .Q(out_27),
    .clk(clk));  // open: clr
  Register #(.width(32)) register_21 (
    .D({register_4_q, register_3_q, register_2_q, register_1_q}), .en(demultiplexer_1_out15), .Q(out_28),
    .clk(clk));  // open: clr
  Register #(.width(32)) register_22 (
    .D({register_4_q, register_3_q, register_2_q, register_1_q}), .en(demultiplexer_1_out16), .Q(out_30),
    .clk(clk));  // open: clr
  Register #(.width(32)) register_23 (
    .D({register_4_q, register_3_q, register_2_q, register_1_q}), .en(demultiplexer_1_out17), .Q(out_31),
    .clk(clk));  // open: clr
  Register #(.width(32)) register_24 (
    .D({register_4_q, register_3_q, register_2_q, register_1_q}), .en(demultiplexer_1_out18), .Q(out_32),
    .clk(clk));  // open: clr
  Register #(.width(32)) register_25 (
    .D({register_4_q, register_3_q, register_2_q, register_1_q}), .en(demultiplexer_1_out19), .Q(out_33),
    .clk(clk));  // open: clr
  Register #(.width(32)) register_26 (
    .D({register_4_q, register_3_q, register_2_q, register_1_q}), .en(demultiplexer_1_out20), .Q(out_34),
    .clk(clk));  // open: clr
  Register #(.width(32)) register_27 (
    .D({register_4_q, register_3_q, register_2_q, register_1_q}), .en(demultiplexer_1_out21), .Q(out_35),
    .clk(clk));  // open: clr
  Register #(.width(32)) register_28 (
    .D({register_4_q, register_3_q, register_2_q, register_1_q}), .en(demultiplexer_1_out22), .Q(out_36),
    .clk(clk));  // open: clr
  Register #(.width(32)) register_29 (
    .D({register_4_q, register_3_q, register_2_q, register_1_q}), .en(demultiplexer_1_out23), .Q(out_37),
    .clk(clk));  // open: clr
  Register #(.width(32)) register_30 (
    .D({register_4_q, register_3_q, register_2_q, register_1_q}), .en(demultiplexer_1_out24), .Q(out_38),
    .clk(clk));  // open: clr
  Register #(.width(32)) register_31 (
    .D({register_4_q, register_3_q, register_2_q, register_1_q}), .en(demultiplexer_1_out25), .Q(out_39),
    .clk(clk));  // open: clr
  Register #(.width(32)) register_32 (
    .D({register_4_q, register_3_q, register_2_q, register_1_q}), .en(demultiplexer_1_out26), .Q(out_40),
    .clk(clk));  // open: clr
  Register #(.width(32)) register_33 (
    .D({register_4_q, register_3_q, register_2_q, register_1_q}), .en(demultiplexer_1_out27), .Q(out_41),
    .clk(clk));  // open: clr
  Register #(.width(32)) register_34 (
    .D({register_4_q, register_3_q, register_2_q, register_1_q}), .en(demultiplexer_1_out28), .Q(out_42),
    .clk(clk));  // open: clr
  Register #(.width(32)) register_35 (
    .D({register_4_q, register_3_q, register_2_q, register_1_q}), .en(demultiplexer_1_out29), .Q(out_43),
    .clk(clk));  // open: clr
  Register #(.width(32)) register_36 (
    .D({register_4_q, register_3_q, register_2_q, register_1_q}), .en(demultiplexer_1_out30), .Q(out_44),
    .clk(clk));  // open: clr
  Register #(.width(32)) register_37 (
    .D({register_4_q, register_3_q, register_2_q, register_1_q}), .en(demultiplexer_1_out31), .Q(out_45),
    .clk(clk));  // open: clr
  Multiplexer #(.select(5), .width(32), .enable("false")) multiplexer_1 (
    .in0(out_13), .in1(out_14), .in2(out_15), .in3(out_16), .in4(out_17), .in5(out_18), .in6(out_19),
    .in7(out_20), .in8(out_21), .in9(out_22), .in10(out_23), .in11(out_24), .in12(out_25), .in13(out_26),
    .in14(out_27), .in15(out_28), .in16(out_30), .in17(out_31), .in18(out_32), .in19(out_33), .in20(out_34),
    .in21(out_35), .in22(out_36), .in23(out_37), .in24(out_38), .in25(out_39), .in26(out_40), .in27(out_41),
    .in28(out_42), .in29(out_43), .in30(out_44), .in31(out_45), .out(Single_row_output),
    .sel(Output_Selector[4:0]));
  // Probe on Output_Selector[4:0]
endmodule

module Keyboard_controller (
  input  [6:0] ASCII_code,
  output [7:0] X,
  output [7:0] Y
);

  wire _0x_y, _0x_y_t, minus_x0y, minus_x_y, minus_x_y_t, or_1_out, or_2_out, or_3_out, or_4_out, or_5_out,
       or_6_out, plus_x0y, plus_x_y, plus_x_y_t;

  Comparator #(.width(7)) comparator_1 (.a(ASCII_code), .b(7'b0110111), .eq(minus_x_y_t));  // open: gt, lt
  Comparator #(.width(7)) comparator_2 (.a(ASCII_code), .b(7'b0110100), .eq(minus_x0y));  // open: gt, lt
  Comparator #(.width(7)) comparator_3 (.a(ASCII_code), .b(7'b0110001), .eq(minus_x_y));  // open: gt, lt
  Comparator #(.width(7)) comparator_4 (.a(ASCII_code), .b(7'b0111000), .eq(_0x_y_t));  // open: gt, lt
  Comparator #(.width(7)) comparator_5 (.a(ASCII_code), .b(7'b0110010), .eq(_0x_y));  // open: gt, lt
  Comparator #(.width(7)) comparator_6 (.a(ASCII_code), .b(7'b0111001), .eq(plus_x_y_t));  // open: gt, lt
  Comparator #(.width(7)) comparator_7 (.a(ASCII_code), .b(7'b0110110), .eq(plus_x0y));  // open: gt, lt
  Comparator #(.width(7)) comparator_8 (.a(ASCII_code), .b(7'b0110011), .eq(plus_x_y));  // open: gt, lt
  or or_1 (or_1_out, minus_x_y_t, minus_x0y, minus_x_y);
  or or_2 (or_2_out, or_1_out, or_3_out);
  or or_3 (or_3_out, plus_x_y_t, plus_x0y, plus_x_y);
  or or_4 (or_4_out, minus_x_y_t, _0x_y_t, plus_x_y_t);
  or or_5 (or_5_out, or_4_out, or_6_out);
  or or_6 (or_6_out, minus_x_y, _0x_y, plus_x_y);
  // Probe on X
  Counter #(.max('h1f)) counter_1 (.load(or_1_out), .count(or_2_out), .Q(X), .clk(or_2_out));  // open: D, carry, clr
  // Probe on Y
  Counter #(.max('h1f)) counter_2 (.load(or_4_out), .count(or_5_out), .Q(Y), .clk(or_5_out));  // open: D, carry, clr

  // Notes on the sheet:
  //   X position
  //   Y position
endmodule
